# Fritzing sketch Eldiven üzerine yapılacak sistem şematiği (saved by Fritzing 1.0.4)
breadboards: 1

parts:
  NRF24L01 = NRF24L01+ Breakout Board
  MPU6050 = InvenSense MPU6050
  Arduino_nano = Arduino Nano (Rev3.0)
  VCC1 = Battery block 9V [internal_resistance=0.1Ω]
  IC1 = 24LC01 [package=THT]
  LED2 = LED - 5mm [color="Red (633nm)" current=0.030A package="5 mm [THT]"]
  S1 = Pushbutton [package="[THT]"]
  S2 = Pushbutton [package="[THT]"]

nets:
  GND: NRF24L01.GND, MPU6050.GND, Arduino_nano.GND, Arduino_nano.A6, VCC1.-, IC1.0V, LED2.cathode, S2.Pin_3, S2.Pin_4
  VCC: NRF24L01.VCC, Arduino_nano.3V3
  N1: NRF24L01.CE, Arduino_nano.D7
  N2: NRF24L01.CS, Arduino_nano.D8
  N3: NRF24L01.SCK, Arduino_nano.D13/SCK
  N4: NRF24L01.MOSI, Arduino_nano.D11/MOSI
  N5: NRF24L01.MISO, Arduino_nano.D12/MISO
  VCC_2: MPU6050.VCC, Arduino_nano.5V, Arduino_nano.A7
  N6: MPU6050.SCL, Arduino_nano.A5
  N7: MPU6050.SDA, Arduino_nano.A4
  N8: MPU6050.XDA, Arduino_nano.A3
  N9: MPU6050.XCL, Arduino_nano.A2, IC1.A2
  N10: MPU6050.AD0, Arduino_nano.A1, IC1.A1
  N11: MPU6050.INT, Arduino_nano.A0, IC1.A0
  N12: Arduino_nano.D1/TX, IC1.WP_-_Write_Protect
  N13: Arduino_nano.D0/RX, Arduino_nano.RESET, IC1.SCL_-_I2C_Clock
  N14: Arduino_nano.D2, IC1.SDA_-_I2C_Data
  N15: Arduino_nano.D3, LED2.anode
  N16: Arduino_nano.D4, S1.Pin_1, S1.Pin_2
  N17: Arduino_nano.D5, S2.Pin_2
  N18: Arduino_nano.VIN, VCC1.+, IC1.+V

notes:
  Eldiven üzerine yapılacak sistem
