# Fritzing sketch araç (saved by Fritzing 1.0.4)

parts:
  L298N1 = L298N DC motor driver
  Parça1 = Arduino Uno (Rev3) - ICSP
  M1 = gear-motor
  M2 = gear-motor
  Parça2 = NRF24L01+ Breakout Board
  VCC1 = 4 x AAA Battery Mount [internal_resistance=0.1Ω]
  VCC2 = Battery block 9V [internal_resistance=0.1Ω]
  HC-SR04_Sensor_1 = HC-SR04 Ultrasonic Distance Sensor

nets:
  N1: L298N1.OUT1, M2.pin_1
  N2: L298N1.OUT2, M2.pin_2
  N3: L298N1.OUT3, M1.pin_2
  N4: L298N1.OUT4, M1.pin_1
  N5: L298N1.12V, VCC1.+
  GND: L298N1.GND, Parça1.GND, Parça2.GND, VCC1.-, VCC2.-
  N6: L298N1.IN1, Parça1.D5_PWM
  N7: L298N1.IN2, Parça1.D6_PWM
  N8: L298N1.IN3, Parça1.D9_PWM
  N9: L298N1.IN4, Parça1.D10_PWM/SS
  N10: Parça1.D8, Parça2.CS
  N11: Parça1.D11_PWM/MOSI, Parça2.MOSI
  N12: Parça1.D12/MISO, Parça2.MISO
  N13: Parça1.D13/SCK, Parça2.SCK
  N14: Parça1.D3_PWM, HC-SR04_Sensor_1.ECHO
  N15: Parça1.D4, HC-SR04_Sensor_1.TRIG
  N16: Parça1.D7, Parça2.CE
  3V3: Parça1.3V3, Parça2.VCC
  5V: Parça1.5V, HC-SR04_Sensor_1.VCC
  VIN: Parça1.VIN, VCC2.+, HC-SR04_Sensor_1.GND

custom parts:
  L298N DC motor driver: 2x DC motor driver with 78M05 positive voltage regulator (7..35 V) L298N: max 46 V, 2 A Set 5 V Enable jumper to enable 5 V regultor (needed for the L298N) and +5 V output at screw terminal or supply external +5 V at screw terminal Set ENA and/or ENB to +5 V to enable motor permanently or supply ENA and/or ENB with PWM signal IN1 and IN2 set rotation directory for motor A (OUT1/OUT2) IN2 and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
